# Fritzing sketch SpaceshipSchematic (saved by Fritzing 0.7.12b)
breadboards: 1

parts:
  Arduino1 = Arduino
  LCD1 = LCD screen
  R1 = Resistor [tolerance=±5% resistance=220 package=THT]
  R2 = Rotary Potentiometer (Small) [maximum_resistance=100kΩ]
  S1 = Pushbutton [package="[THT]"]
  S2 = Pushbutton [package="[THT]"]
  R3 = Resistor [tolerance=±5% resistance=10k package=THT]
  R4 = Resistor [tolerance=±5% resistance=10k package=THT]

nets:
  GND: Arduino1.GND, LCD1.VSS, LCD1.R/W, LCD1.LED-, R2.leg2, R3.Pin_1, R4.Pin_1
  N1: Arduino1.D12, LCD1.RS
  N2: Arduino1.D11, LCD1.E
  N3: Arduino1.D7, S2.Pin_2, R4.Pin_0
  N4: Arduino1.D6, S1.Pin_4, R3.Pin_0
  N5: Arduino1.D5, LCD1.DB4
  N6: Arduino1.D4, LCD1.DB5
  N7: Arduino1.D3, LCD1.DB6
  N8: Arduino1.D2, LCD1.DB7
  +5V: Arduino1.+5V, LCD1.VDD, R1.Pin_0, R2.leg1, S1.Pin_2, S2.Pin_3, S2.Pin_4
  N9: LCD1.V0, R2.wiper
  N10: LCD1.LED+, R1.Pin_1
